# Fritzing sketch schematic (saved by Fritzing 0.9.3b)
circuit board: 8.46667cm x 5.64444cm
breadboards: 1

parts:
  DHT1 = DHT22 Humidity and Temperature Sensor
  WeMos_D1_Mini1 = WeMos D1 Mini
  S1 = SWITCH-MOMENTARY-2 [package=reed_switch_plastic]
  R1 = Resistor [tolerance=±1% resistance=10k package="0402 [SMD]"]

nets:
  VDD: DHT1.VDD, WeMos_D1_Mini1.3V3, S1.2
  N1: DHT1.DATA, WeMos_D1_Mini1.D1
  N2: DHT1.GND, WeMos_D1_Mini1.G, R1.Pin_1
  N3: WeMos_D1_Mini1.D2, S1.1, R1.Pin_0

custom parts:
  WeMos D1 Mini: The D1 mini is a mini wifi board based on ESP-8266EX.
